# Fritzing sketch circut (saved by Fritzing 0.9.0b)
breadboards: 1

parts:
  Arduino_UNO_Rev3 = Arduino Uno (Rev3)
  R1 = Resistor [tolerance=±5% resistance=330 package=THT]
  R2 = Trimmer Potentiometer [maximum_resistance=10kΩ package=THT]
  R3 = Resistor [tolerance=±5% resistance=10k package=THT]
  Speaker = Piezo Speaker

nets:
  N1: Arduino_UNO_Rev3.A0, R2.wiper
  N2: Arduino_UNO_Rev3.D11_PWM/MOSI, R3.Pin_0
  N3: Arduino_UNO_Rev3.GND, R2.leg2, Speaker.pin1
  N4: Arduino_UNO_Rev3.5V, R1.Pin_0
  N5: R1.Pin_1, R2.leg1
  N6: R3.Pin_1, Speaker.pin2
